# Fritzing sketch final 회로도 (saved by Fritzing 0.9.3b)
breadboards: 1

parts:
  부품1 = Arduino Uno (Rev3)
  gyro_IMU_9DOF_v2_0 = 9 Degrees of Freedom - Sensor Stick
  LCD_monitor = LCD screen
  Piezo_Speaker = Piezo Speaker
  U1 = SUP500F [package=sup500f]  # not connected

nets:
  N1: 부품1.A4/SDA, gyro_IMU_9DOF_v2_0.SDA, LCD_monitor.R/W
  N2: 부품1.A5/SCL, gyro_IMU_9DOF_v2_0.SCL, LCD_monitor.RS
  N3: 부품1.D8, Piezo_Speaker.pin2
  5V: 부품1.5V, gyro_IMU_9DOF_v2_0.VCC, LCD_monitor.VDD
  GND: 부품1.GND, gyro_IMU_9DOF_v2_0.GND, LCD_monitor.V0, Piezo_Speaker.pin1
